// Logisim project part1.circ as structural Verilog: 1 circuit, main circuit main
module main (
  input  x,
  input  s,
  input  y,
  output f
);

  wire n7408_1_p2, n7408_1_p3, n7408_1_p6;

  // _7408 7408_1: pin names not known; wires that end beside it: x, n7408_1_p2, n7408_1_p3, s, y, n7408_1_p6
  // _7404 7404_1: pin names not known; wires that end beside it: s, n7408_1_p2
  // _7432 7432_1: pin names not known; wires that end beside it: n7408_1_p3, n7408_1_p6, f

  // Notes on the sheet:
  //   Hshmat Sahak
  //   ECE253 Lab 1 Part 1
endmodule
