// Logisim project part2.circ as structural Verilog: 1 circuit, main circuit main
module main (
  input  a,
  input  b,
  input  c,
  input  d,
  output f
);

  wire n7404_1_p2, n7404_1_p4, n7408_1_p1, n7408_1_p4, n7432_1_p1;

  // _7404 7404_1: pin names not known; wires that end beside it: a, n7404_1_p2, b, n7404_1_p4, c
  // _7408 7408_1: pin names not known; wires that end beside it: n7408_1_p1, n7404_1_p2, n7408_1_p1, n7408_1_p4, n7404_1_p4, d
  // _7432 7432_1: pin names not known; wires that end beside it: n7432_1_p1, n7408_1_p4, n7432_1_p1, f

  // Notes on the sheet:
  //   Hshmat Sahak
  //   ECE253 Lab 1 Part 2
endmodule
