// Logisim project part3.circ as structural Verilog: 1 circuit, main circuit main
module main (
  input  x,
  input  s,
  input  y,
  output f
);

  wire and_1_out, and_2_out, not_1_out;

  not not_1 (not_1_out, s);
  and and_1 (and_1_out, x, not_1_out);
  and and_2 (and_2_out, s, y);
  or or_1 (f, and_1_out, and_2_out);

  // Notes on the sheet:
  //   ECE253 Lab 1 Part 3
  //   Hshmat Sahak
endmodule
