// Logisim project part4.circ as structural Verilog: 1 circuit, main circuit main
module main (
  input  a,
  input  b,
  input  c,
  input  d,
  output f
);

  wire and_1_out, and_2_out, not_1_out, not_2_out, not_3_out;

  not not_1 (not_1_out, a);
  not not_2 (not_2_out, b);
  not not_3 (not_3_out, c);
  and and_1 (and_1_out, not_1_out, not_3_out);
  and and_2 (and_2_out, not_2_out, d);
  or or_1 (f, and_1_out, and_2_out);

  // Notes on the sheet:
  //   Hshmat Sahak
  //   ECE253 Lab 1 Part 4
endmodule
